# Fritzing sketch intval_3_prototype (saved by Fritzing 0.9.3b)
circuit board: 5.28023cm x 2.89878cm
breadboards: 1

parts:
  IC1 = Voltage Regulator [package=to220-igo]
  J5 = screw terminal, 2 pins
  J6 = screw terminal, 2 pins
  J7 = screw terminal, 2 pins
  J8 = screw terminal, 2 pins
  R1 = Resistor [tolerance=±5% resistance=330 package=THT]
  R2 = Resistor [tolerance=±5% resistance=330 package=THT]
  Raspberry_Pi_1 = Raspberry Pi 3 [part_number=RPI-3-V1.2]

nets:
  GND: IC1.GND, J5.pin2, J6.pin2, J7.pin2, Raspberry_Pi_1.GND
  N1: IC1.IN, J5.pin1
  N2: IC1.OUT, Raspberry_Pi_1.5V
  N3: J6.pin1, R1.Pin_1
  N4: J7.pin1, R2.Pin_1
  N5: J8.pin1, Raspberry_Pi_1.GIPO19
  N6: J8.pin2, Raspberry_Pi_1.GIPO13
  N7: R1.Pin_0, Raspberry_Pi_1.GIPO5
  N8: R2.Pin_0, Raspberry_Pi_1.GIPO6
